// Logisim project Nono.circ as structural Verilog: 7 circuits, main circuit main
module main (
  input  RESET
);

  wire clock_1_out, decodeur_1_isjmp, decodeur_1_isload, decodeur_1_regwrite;
  wire [1:0] controle_de_saut_1_pc;
  wire [2:0] decodeur_1_ctrlual;
  wire [3:0] \sélection_de_registre_1_rd , \sélection_de_registre_1_rs , \sélection_de_registre_1_rt_2 ,
       ual_1_flags;
  wire [7:0] adder_1_out, adder_2_out, banc_de_registres_1_rs_2, banc_de_registres_1_rt_2,
       bit_extender_1_out, multiplexer_1_out, multiplexer_2_out, PC_q, ual_1_s;
  wire [15:0] ram_1_data;

  Register PC (.D(multiplexer_2_out), .en(1'b1), .Q(PC_q), .clk(clock_1_out), .clr(RESET));
  Clock clock_1 (.out(clock_1_out));
  Adder adder_1 (.a(PC_q), .b(8'h1), .out(adder_1_out));  // open: cin, cout
  RAM #(.dataWidth(16)) ram_1 (.addr(PC_q), .data(ram_1_data), .clk(clock_1_out));  // open: sel, ld, clr
  decodeur decodeur_1 (
    .regWrite(decodeur_1_regwrite), .isJMP(decodeur_1_isjmp), .isLoad(decodeur_1_isload),
    .ctrlUAL(decodeur_1_ctrlual), .op(ram_1_data[15:12]));
  Banc_de_registres banc_de_registres_1 (
    .valin(multiplexer_1_out), .rd(\sélection_de_registre_1_rd ), .regWrite(decodeur_1_regwrite),
    .RESET(RESET), .Rs_2(banc_de_registres_1_rs_2), .Rt_2(banc_de_registres_1_rt_2),
    .rt(\sélection_de_registre_1_rt_2 ), .rs(\sélection_de_registre_1_rs ), .Horloge(clock_1_out));
  Multiplexer #(.width(8)) multiplexer_1 (
    .in0(ram_1_data[7:0]), .in1(ual_1_s), .out(multiplexer_1_out), .sel(decodeur_1_isload));  // open: en
  assign bit_extender_1_out = {{4{1'b0}}, ram_1_data[3:0]};  // Bit_Extender bit_extender_1
  \sélection_de_registre  \sélection_de_registre_1  (
    .rd_rs(ram_1_data[11:8]), .rs_rt(ram_1_data[7:4]), .rt(ram_1_data[3:0]), .isJMP(decodeur_1_isjmp),
    .rd(\sélection_de_registre_1_rd ), .rs(\sélection_de_registre_1_rs ),
    .rt_2(\sélection_de_registre_1_rt_2 ));
  Multiplexer #(.select(2), .width(8)) multiplexer_2 (
    .in0(adder_1_out), .in1({8{1'b1}}), .in3(adder_2_out), .out(multiplexer_2_out),
    .sel(controle_de_saut_1_pc));  // open: in2, en
  Adder adder_2 (.a(adder_1_out), .b(bit_extender_1_out), .out(adder_2_out));  // open: cin, cout
  UAL ual_1 (
    .A(banc_de_registres_1_rs_2), .B(banc_de_registres_1_rt_2), .ctrlUAL(decodeur_1_ctrlual), .S(ual_1_s),
    .flags(ual_1_flags));
  Controle_de_saut controle_de_saut_1 (.op(ram_1_data[15:12]), .PC(controle_de_saut_1_pc), .flags(ual_1_flags));
endmodule

module decodeur (
  input  [3:0] op,
  output isLoad,
  output regWrite,
  output isJMP,
  output [2:0] ctrlUAL
);

  wire not_2_out;

  and and_1 (isLoad, op[3], ~op[2], op[1], op[0]);  // AND_Gate
  not not_1 (regWrite, op[2]);
  Multiplexer #(.width(3)) multiplexer_1 (
    .in0({2'b00, op[2]}), .in1({op[3], op[1:0]}), .out(ctrlUAL), .sel(not_2_out));  // open: en
  not not_2 (not_2_out, op[2]);

  assign isJMP = op[2];
endmodule

module UAL (
  input  [7:0] A,
  input  [7:0] B,
  input  [2:0] ctrlUAL,
  output [7:0] S,
  output [3:0] flags
);

  wire adder_1_cout, subtractor_1_bout;
  wire [7:0] adder_1_out, AND_out, NOT_out, OR_out, shifter_1_out, shifter_2_out, subtractor_1_out;

  Adder adder_1 (.a(A), .b(B), .out(adder_1_out), .cout(adder_1_cout));  // open: cin
  or CF (flags[3], subtractor_1_bout, adder_1_cout);
  Subtractor subtractor_1 (.a(A), .b(B), .out(subtractor_1_out), .bout(subtractor_1_bout));  // open: bin
  Multiplexer #(.select(3), .width(8)) multiplexer_1 (
    .in0(adder_1_out), .in1(subtractor_1_out), .in2(OR_out), .in3(AND_out), .in4(NOT_out),
    .in5(shifter_1_out), .in6(shifter_2_out), .out({flags[1], S[6:0]}), .sel(ctrlUAL));  // open: in7, en
  assign OR_out = B | A;  // OR_Gate OR, 8 bits wide
  and ZF (flags[2], ~S[0], ~S[1], ~S[2], ~S[3], ~S[4], ~S[5], ~S[6], ~flags[1]);  // AND_Gate
  assign AND_out = B & A;  // AND_Gate AND, 8 bits wide
  assign NOT_out = ~A;  // NOT_Gate NOT, 8 bits wide
  Shifter shifter_1 (.in(A), .\dist (B[2:0]), .out(shifter_1_out));
  Shifter #(.shift("lr")) shifter_2 (.in(A), .\dist (B[2:0]), .out(shifter_2_out));
  and OF (flags[0], B[7], A[7]);

  assign S[7] = flags[1];

  // Notes on the sheet:
  //   add
  //   sub
  //   S
  //   SF
  //   <<
  //   >>
endmodule

module Controle_de_saut (
  input  [3:0] op,
  input  [3:0] flags,
  output [1:0] PC
);

  wire and_1_out, and_2_out, and_3_out, and_4_out, and_5_out, and_6_out, and_7_out, and_8_out, e1_out,
       not_1_out;

  and and_1 (and_1_out, ~op[3], ~op[1], op[0]);  // AND_Gate
  and and_2 (and_2_out, ~op[3], op[0], ~flags[2], ~flags[1]);  // AND_Gate
  and and_3 (and_3_out, ~op[3], op[1], ~op[0], flags[2]);  // AND_Gate
  and and_4 (and_4_out, op[3], op[1], ~op[0], ~flags[2], ~flags[1]);  // AND_Gate
  and and_5 (and_5_out, op[3], op[0], ~flags[2], flags[1]);  // AND_Gate
  and and_6 (and_6_out, ~op[1], ~flags[2], ~flags[1]);  // AND_Gate
  or e1 (e1_out, and_1_out, and_2_out, and_3_out, and_4_out, and_5_out, and_6_out, op[3]);
  and and_7 (and_7_out, op[2], e1_out);
  and and_8 (and_8_out, ~op[0], ~op[1], op[2], ~op[3]);  // AND_Gate
  not not_1 (not_1_out, and_8_out);
  and and_9 (PC[1], and_7_out, not_1_out);
  and and_10 (PC[0], and_7_out, op[2]);

  // Notes on the sheet:
  //   Halt
  //   e0
endmodule

module Banc_de_registres (
  input  [7:0] valin,
  input  [3:0] rd,
  input  [3:0] rs,
  input  [3:0] rt,
  input  Horloge,
  input  regWrite,
  input  RESET,
  output [7:0] Rs_2,
  output [7:0] Rt_2
);

  wire and_1_out, and_2_out, and_3_out, and_4_out, and_5_out, and_6_out, and_7_out, and_8_out, and_9_out,
       and_10_out, and_11_out, and_12_out, and_13_out, and_14_out, and_15_out, and_16_out, decodeur_rd_1_r0,
       decodeur_rd_1_r1, decodeur_rd_1_r2, decodeur_rd_1_r3, decodeur_rd_1_r4, decodeur_rd_1_r5,
       decodeur_rd_1_r6, decodeur_rd_1_r7, decodeur_rd_1_r8, decodeur_rd_1_r9, decodeur_rd_1_r10,
       decodeur_rd_1_r11, decodeur_rd_1_r12, decodeur_rd_1_r13, decodeur_rd_1_r14, decodeur_rd_1_r15;
  wire [7:0] r0_q, r1_q, r2_q, r3_q, r4_q, r5_q, r6_q, r7_q, r8_q, r9_q, r10_q, r11_q, r12_q, r13_q, r14_q,
       r15_q;

  decodeur_rd decodeur_rd_1 (
    .in_1(rd), .r0(decodeur_rd_1_r0), .r1(decodeur_rd_1_r1), .r2(decodeur_rd_1_r2), .r3(decodeur_rd_1_r3),
    .r4(decodeur_rd_1_r4), .r5(decodeur_rd_1_r5), .r6(decodeur_rd_1_r6), .r7(decodeur_rd_1_r7),
    .r8(decodeur_rd_1_r8), .r9(decodeur_rd_1_r9), .r10(decodeur_rd_1_r10), .r11(decodeur_rd_1_r11),
    .r12(decodeur_rd_1_r12), .r13(decodeur_rd_1_r13), .r14(decodeur_rd_1_r14), .r15(decodeur_rd_1_r15));
  Register r15 (.D(valin), .en(and_1_out), .Q(r15_q), .clk(Horloge), .clr(RESET));
  and and_1 (and_1_out, decodeur_rd_1_r15, regWrite);
  Register r11 (.D(valin), .en(and_2_out), .Q(r11_q), .clk(Horloge), .clr(RESET));
  and and_2 (and_2_out, decodeur_rd_1_r11, regWrite);
  Register r7 (.D(valin), .en(and_3_out), .Q(r7_q), .clk(Horloge), .clr(RESET));
  and and_3 (and_3_out, decodeur_rd_1_r7, regWrite);
  Register r3 (.D(valin), .en(and_4_out), .Q(r3_q), .clk(Horloge), .clr(RESET));
  and and_4 (and_4_out, decodeur_rd_1_r3, regWrite);
  and and_5 (and_5_out, decodeur_rd_1_r14, regWrite);
  and and_6 (and_6_out, decodeur_rd_1_r10, regWrite);
  and and_7 (and_7_out, decodeur_rd_1_r6, regWrite);
  and and_8 (and_8_out, decodeur_rd_1_r2, regWrite);
  Register r14 (.D(valin), .en(and_5_out), .Q(r14_q), .clk(Horloge), .clr(RESET));
  Register r10 (.D(valin), .en(and_6_out), .Q(r10_q), .clk(Horloge), .clr(RESET));
  Register r6 (.D(valin), .en(and_7_out), .Q(r6_q), .clk(Horloge), .clr(RESET));
  Register r2 (.D(valin), .en(and_8_out), .Q(r2_q), .clk(Horloge), .clr(RESET));
  and and_9 (and_9_out, decodeur_rd_1_r13, regWrite);
  and and_10 (and_10_out, decodeur_rd_1_r9, regWrite);
  and and_11 (and_11_out, decodeur_rd_1_r5, regWrite);
  and and_12 (and_12_out, decodeur_rd_1_r1, regWrite);
  Register r13 (.D(valin), .en(and_9_out), .Q(r13_q), .clk(Horloge), .clr(RESET));
  Register r9 (.D(valin), .en(and_10_out), .Q(r9_q), .clk(Horloge), .clr(RESET));
  Register r5 (.D(valin), .en(and_11_out), .Q(r5_q), .clk(Horloge), .clr(RESET));
  Register r1 (.D(valin), .en(and_12_out), .Q(r1_q), .clk(Horloge), .clr(RESET));
  Register r12 (.D(valin), .en(and_13_out), .Q(r12_q), .clk(Horloge), .clr(RESET));
  and and_13 (and_13_out, decodeur_rd_1_r12, regWrite);
  Register r8 (.D(valin), .en(and_14_out), .Q(r8_q), .clk(Horloge), .clr(RESET));
  and and_14 (and_14_out, decodeur_rd_1_r8, regWrite);
  Register r4 (.D(valin), .en(and_15_out), .Q(r4_q), .clr(RESET));  // open: clk
  and and_15 (and_15_out, decodeur_rd_1_r4, regWrite);
  Register r0 (.D(valin), .en(and_16_out), .Q(r0_q), .clk(Horloge), .clr(RESET));
  and and_16 (and_16_out, decodeur_rd_1_r0, regWrite);
  Multiplexer #(.select(4), .width(8)) multiplexer_1 (
    .in0(r0_q), .in1(r1_q), .in2(r2_q), .in3(r3_q), .in4(r4_q), .in5(r5_q), .in6(r6_q), .in7(r7_q),
    .in8(r8_q), .in9(r9_q), .in10(r10_q), .in11(r11_q), .in12(r12_q), .in13(r13_q), .in14(r14_q),
    .in15(r15_q), .out(Rt_2), .sel(rt));  // open: en
  Multiplexer #(.select(4), .width(8)) multiplexer_2 (
    .in0(r0_q), .in1(r1_q), .in2(r2_q), .in3(r3_q), .in4(r4_q), .in5(r5_q), .in6(r6_q), .in7(r7_q),
    .in8(r8_q), .in9(r9_q), .in10(r10_q), .in11(r11_q), .in12(r12_q), .in13(r13_q), .in14(r14_q),
    .in15(r15_q), .out(Rs_2), .sel(rs));  // open: en
endmodule

module decodeur_rd (
  input  [3:0] in_1,
  output r0,
  output r1,
  output r2,
  output r3,
  output r4,
  output r5,
  output r6,
  output r7,
  output r8,
  output r9,
  output r10,
  output r11,
  output r12,
  output r13,
  output r14,
  output r15
);

  and u_r0 (r0, ~in_1[3], ~in_1[2], ~in_1[1], ~in_1[0]);  // AND_Gate
  and u_r1 (r1, ~in_1[3], ~in_1[2], ~in_1[1], in_1[0]);  // AND_Gate
  and u_r2 (r2, ~in_1[3], ~in_1[2], in_1[1], ~in_1[0]);  // AND_Gate
  and u_r3 (r3, ~in_1[3], ~in_1[2], in_1[1], in_1[0]);  // AND_Gate
  and u_r4 (r4, ~in_1[3], in_1[2], ~in_1[1], ~in_1[0]);  // AND_Gate
  and u_r5 (r5, ~in_1[3], in_1[2], ~in_1[1], in_1[0]);  // AND_Gate
  and u_r6 (r6, ~in_1[3], in_1[2], in_1[1], ~in_1[0]);  // AND_Gate
  and u_r7 (r7, ~in_1[3], in_1[2], in_1[1], in_1[0]);  // AND_Gate
  and u_r8 (r8, in_1[3], ~in_1[2], ~in_1[1], ~in_1[0]);  // AND_Gate
  and u_r10 (r10, in_1[3], ~in_1[2], in_1[1], ~in_1[0]);  // AND_Gate
  and u_r9 (r9, in_1[3], ~in_1[2], ~in_1[1], in_1[0]);  // AND_Gate
  and u_r12 (r12, in_1[3], in_1[2], ~in_1[1], ~in_1[0]);  // AND_Gate
  and u_r11 (r11, in_1[3], ~in_1[2], in_1[1], in_1[0]);  // AND_Gate
  and u_r13 (r13, in_1[3], in_1[2], ~in_1[1], in_1[0]);  // AND_Gate
  and u_r15 (r15, in_1[3], in_1[2], in_1[1], in_1[0]);
  and u_r14 (r14, in_1[3], in_1[2], in_1[1], ~in_1[0]);  // AND_Gate
endmodule

module \sélection_de_registre  (
  input  [3:0] rd_rs,
  input  [3:0] rs_rt,
  input  [3:0] rt,
  input  isJMP,
  output [3:0] rd,
  output [3:0] rs,
  output [3:0] rt_2
);

  wire not_1_out, not_2_out;

  not not_1 (not_1_out, isJMP);
  Multiplexer #(.width(4)) multiplexer_1 (.in0(rd_rs), .in1(rs_rt), .out(rs), .sel(not_1_out));  // open: en
  Multiplexer #(.width(4)) multiplexer_2 (.in0(rs_rt), .in1(rt), .out(rt_2), .sel(not_2_out));  // open: en
  not not_2 (not_2_out, isJMP);

  assign rd = rd_rs;
endmodule
