// Logisim project UAL.circ as structural Verilog
module decodeur (
  input  [3:0] op,
  output isLoad,
  output regWrite,
  output isJMP,
  output [2:0] ctrlUAL
);

  wire and_2_out, not_1_out, not_2_out;

  and and_1 (isLoad, op[3], ~op[2], op[1], op[0]);  // AND_Gate
  and and_2 (and_2_out, ~op[3], op[2], ~op[1], ~op[0]);  // AND_Gate
  not not_1 (not_1_out, and_2_out);
  and and_3 (isJMP, op[2], not_1_out);
  and and_4 (regWrite, ~isLoad, ~isJMP);  // AND_Gate
  Multiplexer #(.width(3)) multiplexer_1 (
    .in0({2'b00, isJMP}), .in1(op[2:0]), .out(ctrlUAL), .sel(not_2_out));  // open: en
  not not_2 (not_2_out, isJMP);
endmodule

module UAL (
  input  [7:0] A,
  input  [7:0] B,
  input  [2:0] ctrlUAL,
  output [7:0] S,
  output [3:0] flags
);

  wire adder_1_cout, subtractor_1_bout;
  wire [7:0] adder_1_out, AND_out, NOT_out, OR_out, shifter_1_out, shifter_2_out, subtractor_1_out;

  Adder adder_1 (.a(A), .b(B), .out(adder_1_out), .cout(adder_1_cout));  // open: cin
  or CF (flags[3], subtractor_1_bout, adder_1_cout);
  Subtractor subtractor_1 (.a(A), .b(B), .out(subtractor_1_out), .bout(subtractor_1_bout));  // open: bin
  Multiplexer #(.select(3), .width(8)) multiplexer_1 (
    .in0(adder_1_out), .in1(subtractor_1_out), .in2(OR_out), .in3(AND_out), .in4(NOT_out),
    .in5(shifter_1_out), .in6(shifter_2_out), .out({flags[1], S[6:0]}), .sel(ctrlUAL));  // open: in7, en
  assign OR_out = B | A;  // OR_Gate OR, 8 bits wide
  and ZF (flags[2], ~S[0], ~S[1], ~S[2], ~S[3], ~S[4], ~S[5], ~S[6], ~flags[1]);  // AND_Gate
  assign AND_out = B & A;  // AND_Gate AND, 8 bits wide
  assign NOT_out = ~A;  // NOT_Gate NOT, 8 bits wide
  Shifter shifter_1 (.in(A), .\dist (3'b001), .out(shifter_1_out));
  Shifter #(.shift("lr")) shifter_2 (.in(A), .\dist (3'b001), .out(shifter_2_out));
  or OF (flags[0], A[7], A[0]);

  assign S[7] = flags[1];

  // Notes on the sheet:
  //   add
  //   sub
  //   S
  //   SF
  //   <<
  //   >>
endmodule

module Controle_de_saut (
  input  [3:0] op,
  input  [3:0] flags
);
endmodule
